# Fritzing sketch UARTGUIRpasberripipico (saved by Fritzing 0.9.3b)
breadboards: 1

parts:
  Mod1 = Raspberry Pi Pico  # not connected
  T1 = LM35 Temperature Sensor [package="TO92 [THT]"]
  U1 = LM 358 Dual Op-Amp [package="SO 08 [SMD]"]  # not connected
  Power_plug1 = Power plug
  SERVO1 = Tower Pro SG90 servo [part_number=101246]  # not connected
  SERVO2 = Tower Pro SG90 servo [part_number=101246]
  USBUART1 = CP2102 USB UART Breakout

nets:
  GND: T1.GND, Power_plug1.GND, SERVO2.GND, USBUART1.GND
  VCC: Power_plug1.VCC, SERVO2.+5V

notes:
  Pinza
  Base
  Fuente externa 5V

custom parts:
  Raspberry Pi Pico: Raspberry Pi Pico. Based around the RP2040 microcontroller the Pico is a low cost microcontroller device bringing Raspberry Pi quality, cost, and easy of use to the microcontroller space. Jan 2021, Split part in to two versions: tht (this one) and SMD. This one will drill holes for a .1 in header in pcb to allow plugging in the module as well as providing pads to solder the module to the top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
  Tower Pro SG90 servo: Original file by John De Cristofaro http://www.adafruit.com/products/1449 Adafruit Feedback Servo (Small) Edited by: e-radionica.com 28/9/2015
  CP2102 USB UART Breakout: CP2102 Usb Uart Breakout Board with Battery
